# Fritzing sketch pcb_scheme (saved by Fritzing 0.9.3b)
breadboards: 1

parts:
  R1 = Rotary Potentiometer (Small) [maximum_resistance=100kΩ package=THT]
  R2 = Rotary Potentiometer (Small) [maximum_resistance=100kΩ package=THT]
  R3 = Rotary Potentiometer (Small) [maximum_resistance=100kΩ package=THT]
  R4 = Resistor [tolerance=±5% resistance=220 package=THT]
  J1 = Piezo Speaker
  LED1 = LED - 5mm [color="Red (633nm)" package="5 mm [THT]"]
  Componente1 = Arduino Uno (Rev3)
  J2 = Basic Servo
  LED2 = LED - 5mm [color="Red (633nm)" package="5 mm [THT]"]

nets:
  GND: R1.leg1, R2.leg1, R3.leg1, R4.Pin_1, J1.pin1, Componente1.GND, J2.gnd, LED2.cathode
  N1: R1.wiper, Componente1.A2
  5V: R1.leg2, R2.leg2, R3.leg2, Componente1.5V, J2.vcc, LED2.anode
  N2: R2.wiper, Componente1.A1
  N3: R3.wiper, Componente1.A0
  N4: R4.Pin_0, LED1.anode
  N5: J1.pin2, Componente1.D11_PWM/MOSI
  N6: LED1.cathode, Componente1.D12/MISO
  N7: Componente1.AREF, J2.pulse

notes:
  Conection
