# Fritzing sketch pcb_scheme_rpi (saved by Fritzing 0.9.3b)

parts:
  CAMERA1 = TTL Serial JPEG Camera
  USBTTL1 = USB TTL Serial Cable
  Raspberry_Pi_1 = Raspberry Pi 3 [part_number=RPI-3-V1.2]  # not connected
  Componente1 = Arduino BT  # not connected

nets:
  N1: CAMERA1.TX, USBTTL1.TX
  N2: CAMERA1.RX, USBTTL1.RX
  GND: CAMERA1.GND, USBTTL1.GND
  5V: CAMERA1.5V, USBTTL1.5V

custom parts:
  TTL Serial JPEG Camera: TTL Serial JPEG Camera with NTSC Out
